// Logisim project adder_subtractor.circ as structural Verilog: 4 circuits, main circuit Half Adder
module Half_Adder (
  input  A,
  input  B,
  output Carry,
  output Sum
);

  and and_1 (Carry, B, A);
  xor xor_1 (Sum, B, A);

  // Notes on the sheet:
  //   Half Adder
endmodule

module Full_Adder (
  input  B,
  input  A,
  input  Cin,
  output Sum,
  output Cout
);

  wire and_1_out, and_2_out, xor_1_out;

  xor xor_1 (xor_1_out, B, A);
  and and_1 (and_1_out, B, A);
  xor xor_2 (Sum, xor_1_out, Cin);
  and and_2 (and_2_out, Cin, xor_1_out);
  or or_1 (Cout, and_2_out, and_1_out);

  // Notes on the sheet:
  //   Full Adder
endmodule

module _4_bit_Full_Adder (
  input  Cin,
  input  [3:0] A,
  input  [3:0] B,
  output [3:0] Sum,
  output Cout
);

  wire Full_Adder_2_cout, Full_Adder_3_cout, Full_Adder_cout;

  Full_Adder Full_Adder (.B(B[0]), .A(A[0]), .Cin(Cin), .Sum(Sum[0]), .Cout(Full_Adder_cout));
  Full_Adder Full_Adder_2 (.B(B[1]), .A(A[1]), .Cin(Full_Adder_cout), .Sum(Sum[1]), .Cout(Full_Adder_2_cout));
  Full_Adder Full_Adder_3 (.B(B[2]), .A(A[2]), .Cin(Full_Adder_2_cout), .Sum(Sum[2]), .Cout(Full_Adder_3_cout));
  Full_Adder Full_Adder_4 (.B(B[3]), .A(A[3]), .Cin(Full_Adder_3_cout), .Sum(Sum[3]), .Cout(Cout));
endmodule

module Adder_Subtractor (
  input  Add_Subtract,
  input  [3:0] B,
  input  [3:0] A,
  output [3:0] Sum,
  output Cout
);

  wire [3:0] xor_1_out;

  xor xor_1 (xor_1_out[0], B[0], Add_Subtract);
  xor xor_2 (xor_1_out[1], B[1], Add_Subtract);
  xor xor_3 (xor_1_out[2], B[2], Add_Subtract);
  xor xor_4 (xor_1_out[3], B[3], Add_Subtract);
  _4_bit_Full_Adder _4_bit_Adder (.Cin(Add_Subtract), .A(A), .B(xor_1_out), .Sum(Sum), .Cout(Cout));
endmodule
