// Logisim project ex2.circ as structural Verilog: 2 circuits, main circuit part1
module part1 (
  input  A,
  input  B,
  input  C,
  input  D,
  output O
);

  wire and_1_out, and_2_out, and_3_out, not_1_out, not_2_out, not_3_out, not_4_out;

  not not_1 (not_1_out, D);
  not not_2 (not_2_out, A);
  not not_3 (not_3_out, C);
  not not_4 (not_4_out, B);
  and and_1 (and_1_out, not_1_out, not_2_out);
  and and_2 (and_2_out, not_3_out, not_4_out);
  and and_3 (and_3_out, D, C, A);
  or or_1 (O, and_1_out, and_2_out, and_3_out);

  // Notes on the sheet:
  //   F(a, b, c, d) = a'd' + b'c' + acd
endmodule

module part2 (
  input  D,
  input  [2:0] A_B_C,
  input  E,
  output O
);

  wire not_1_out, not_2_out, not_3_out;

  not not_1 (not_1_out, D);
  not not_2 (not_2_out, D);
  not not_3 (not_3_out, D);
  Multiplexer #(.select(3)) multiplexer_1 (
    .in0(1'b1), .in1(not_1_out), .in2(not_2_out), .in3(not_3_out), .in4(1'b1), .in5(D), .in6(1'b0), .in7(D),
    .out(O), .sel(A_B_C), .en(E));

  // Notes on the sheet:
  //   F(a, b, c, d) = a'd' + b'c' + acd
endmodule
