// Logisim project ex1.circ as structural Verilog: 3 circuits, main circuit ex1
module ex1 (
  input  A,
  input  B,
  output F1,
  output Aout,
  output F2
);

  wire and_1_out, or_1_out;

  and and_1 (and_1_out, A, B);
  or or_1 (or_1_out, B, A);
  or or_2 (F1, and_1_out, A);
  and and_2 (F2, A, or_1_out);

  assign Aout = A;

  // Notes on the sheet:
  //   F1(A, B) = A + A * B = A
  //   F2(A, B) = A  * ( A +  B) = A
endmodule

module ex2 (
  input  A,
  input  B,
  output F1,
  output Aout,
  output F2
);

  wire and_1_out, or_1_out;

  and and_1 (and_1_out, A, B);
  or or_1 (or_1_out, B, A);
  or or_2 (F1, and_1_out, A);
  and and_2 (F2, A, or_1_out);

  assign Aout = A;

  // Notes on the sheet:
  //   F(A, B) = A + A * B = A
  //   Fdual(A, B) = A  * ( A +  B) = A
endmodule

module ex3 (
  input  A,
  input  B,
  input  C,
  output F,
  output F_prime
);

  wire and_1_out, and_2_out, not_1_out, not_2_out, not_3_out, or_1_out, or_2_out;

  not not_1 (not_1_out, A);
  not not_2 (not_2_out, A);
  not not_3 (not_3_out, B);
  and and_1 (and_1_out, A, B);
  and and_2 (and_2_out, C, not_1_out);
  or or_1 (or_1_out, not_2_out, not_3_out);
  or or_2 (or_2_out, A, C);
  or or_3 (F, and_1_out, and_2_out);
  and and_3 (F_prime, or_1_out, or_2_out);

  // Notes on the sheet:
  //   F(A, B, C) = (A * B) + (A' * C)
  //   F'(A, B, C) = (A' + B') * (A + C')
endmodule
