// Logisim project latches_and_flip_flops.circ as structural Verilog: 16 circuits, main circuit S - R Latch (NOR)
module S___R_Latch__NOR (
  input  R,
  input  S,
  output Q,
  output Qnot
);

  nor nor_1 (Q, R, Qnot);
  nor nor_2 (Qnot, Q, S);

  // Notes on the sheet:
  //   S - R Latch (NOR)
endmodule

module S___R_Latch__NAND (
  input  S,
  input  R,
  output Q,
  output Q_prime
);

  nand nand_1 (Q, S, Q_prime);
  nand nand_2 (Q_prime, Q, R);

  // Notes on the sheet:
  //   S - R Latch (NAND)
endmodule

module S___R_Latch_Enable__NOR (
  input  R,
  input  E,
  input  S,
  output Q,
  output Q_prime
);

  wire and_1_out, and_2_out;

  and and_1 (and_1_out, R, E);
  and and_2 (and_2_out, E, S);
  nor nor_1 (Q, and_1_out, Q_prime);
  nor nor_2 (Q_prime, Q, and_2_out);

  // Notes on the sheet:
  //   S - R Latch Enable (NOR)
endmodule

module S___R_Latch_Enable__NAND (
  input  S,
  input  E,
  input  R,
  output Q,
  output Qnot
);

  wire nand_1_out, nand_4_out;

  nand nand_1 (nand_1_out, S, E);
  nand nand_2 (Q, nand_1_out, Qnot);
  nand nand_3 (Qnot, Q, nand_4_out);
  nand nand_4 (nand_4_out, E, R);

  // Notes on the sheet:
  //   S - R Latch Enable (NAND)
endmodule

module D_Latch__NOR (
  input  D,
  input  E,
  output Q_prime,
  output Q
);

  wire and_1_out, and_2_out, not_1_out;

  and and_1 (and_1_out, D, E);
  not not_1 (not_1_out, D);
  and and_2 (and_2_out, not_1_out, E);
  nor nor_1 (Q_prime, and_1_out, Q);
  nor nor_2 (Q, Q_prime, and_2_out);

  // Notes on the sheet:
  //   D Latch (NOR)
endmodule

module D_Latch__NAND (
  input  D,
  input  E,
  output Q,
  output Q_prime
);

  wire nand_1_out, nand_4_out;

  nand nand_1 (nand_1_out, D, E);
  nand nand_2 (Q, nand_1_out, Q_prime);
  nand nand_3 (Q_prime, Q, nand_4_out);
  nand nand_4 (nand_4_out, nand_1_out, E);

  // Notes on the sheet:
  //   D Latch (NAND)
endmodule

module D_Flip_Flop__Negative (
  input  D,
  input  CLK,
  output Q,
  output Q_prime
);

  wire D_Latch_q, not_1_out;

  D_Latch__NAND D_Latch (.D(D), .E(CLK), .Q(D_Latch_q));  // open: Q_prime
  not not_1 (not_1_out, CLK);
  D_Latch__NAND D_Latch_2 (.D(D_Latch_q), .E(not_1_out), .Q(Q), .Q_prime(Q_prime));

  // Notes on the sheet:
  //   D Flip Flop (Negative)
endmodule

module D_Flip_Flop__Positive (
  input  D,
  input  CLK,
  output Q,
  output Q_prime
);

  wire D_Latch_q, not_1_out, not_2_out;

  not not_1 (not_1_out, CLK);
  D_Latch__NAND D_Latch (.D(D), .E(not_1_out), .Q(D_Latch_q));  // open: Q_prime
  not not_2 (not_2_out, not_1_out);
  D_Latch__NAND D_Latch_2 (.D(D_Latch_q), .E(not_2_out), .Q(Q), .Q_prime(Q_prime));

  // Notes on the sheet:
  //   D Flip Flop (Positive)
endmodule

module J___K_Latch__NOR (
  input  K,
  input  J,
  output Q,
  output Q_prime
);

  wire and_1_out, and_2_out;

  and and_1 (and_1_out, Q, K);
  and and_2 (and_2_out, J, Q_prime);
  nor nor_1 (Q, and_1_out, Q_prime);
  nor nor_2 (Q_prime, Q, and_2_out);

  // Notes on the sheet:
  //   J - K Latch (NOR)
endmodule

module J___K_Latch__NAND (
  input  J,
  input  K,
  output Q,
  output Q_prime
);

  wire nand_1_out, nand_2_out;

  nand nand_1 (nand_1_out, Q_prime, J);
  nand nand_2 (nand_2_out, K, Q);
  nand nand_3 (Q, nand_1_out, Q_prime);
  nand nand_4 (Q_prime, Q, nand_2_out);

  // Notes on the sheet:
  //   J - K Latch (NAND)
endmodule

module J___K_Flip_Flop__NOR (
  input  K,
  input  J,
  output Q,
  output Q_prime
);

  wire and_1_out, and_2_out, CLK_out;

  and and_1 (and_1_out, Q, K, CLK_out);
  Clock CLK (.out(CLK_out));
  and and_2 (and_2_out, CLK_out, J, Q_prime);
  nor nor_1 (Q, and_1_out, Q_prime);
  nor nor_2 (Q_prime, Q, and_2_out);

  // Notes on the sheet:
  //   J - K Flip Flop (NOR)
endmodule

module J___K_Flip_Flop__NAND (
  input  J,
  input  K,
  output Q,
  output Q_prime
);

  wire CLK_out, nand_1_out, nand_2_out;

  nand nand_1 (nand_1_out, Q_prime, J, CLK_out);
  Clock CLK (.out(CLK_out));
  nand nand_2 (nand_2_out, CLK_out, K, Q);
  nand nand_3 (Q, nand_1_out, Q_prime);
  nand nand_4 (Q_prime, Q, nand_2_out);

  // Notes on the sheet:
  //   J - K Flip Flop (NAND)
endmodule

module T_Flip_Flop__NOR (
  input  J,
  output Q,
  output Q_prime
);

  wire and_1_out, and_2_out, and_3_out, CLK_out, not_1_out;

  Clock CLK (.out(CLK_out));
  and and_1 (and_1_out, CLK_out, not_1_out);
  not not_1 (not_1_out, CLK_out);
  and and_2 (and_2_out, Q, J, and_1_out);
  and and_3 (and_3_out, and_1_out, J, Q_prime);
  nor nor_1 (Q, and_2_out, Q_prime);
  nor nor_2 (Q_prime, Q, and_3_out);

  // Notes on the sheet:
  //   Pos Edge
  //   T Flip Flop (NOR)
endmodule

module Shift_Register (
  input  D
);

  wire clock_1_out, d_flip_flop_negative_1_q, d_flip_flop_negative_2_q, d_flip_flop_negative_3_q,
       d_flip_flop_negative_4_q;

  Clock clock_1 (.out(clock_1_out));
  LED led_1 (.in(d_flip_flop_negative_3_q));
  LED led_2 (.in(d_flip_flop_negative_1_q));
  D_Flip_Flop__Negative d_flip_flop_negative_1 (
    .D(D), .CLK(clock_1_out), .Q(d_flip_flop_negative_1_q));  // open: Q_prime
  LED led_3 (.in(d_flip_flop_negative_2_q));
  D_Flip_Flop__Negative d_flip_flop_negative_2 (
    .D(d_flip_flop_negative_3_q), .CLK(clock_1_out), .Q(d_flip_flop_negative_2_q));  // open: Q_prime
  D_Flip_Flop__Negative d_flip_flop_negative_3 (
    .D(d_flip_flop_negative_1_q), .CLK(clock_1_out), .Q(d_flip_flop_negative_3_q));  // open: Q_prime
  LED led_4 (.in(d_flip_flop_negative_4_q));
  D_Flip_Flop__Negative d_flip_flop_negative_4 (
    .D(d_flip_flop_negative_2_q), .CLK(clock_1_out), .Q(d_flip_flop_negative_4_q));  // open: Q_prime
endmodule

module Counter_to_5 (
  input  [3:0] in_1
);

  wire and_1_out, clock_1_out, not_1_out, not_2_out, not_3_out;
  wire [3:0] counter_1_q;

  not not_1 (not_1_out, and_1_out);
  Hex_Digit_Display hex_digit_display_1 (.value(counter_1_q));  // open: dp
  Counter #(.width(4), .max('hf)) counter_1 (
    .load(and_1_out), .D(in_1), .count(not_1_out), .Q(counter_1_q), .clk(clock_1_out));  // open: carry, clr
  Clock clock_1 (.out(clock_1_out));
  not not_2 (not_2_out, counter_1_q[1]);
  not not_3 (not_3_out, counter_1_q[3]);
  and and_1 (and_1_out, counter_1_q[0], not_2_out, counter_1_q[2], not_3_out);
endmodule

module Pulse_Generator (
  input  [7:0] in_1,
  input  in_2,
  input  in_3
);

  wire button_1_out, clock_1_out, shift_register_1_out;

  Shift_Register_part shift_register_1 (
    .shift(in_3), .in(shift_register_1_out), .clk(clock_1_out), .out(shift_register_1_out), .load(in_2),
    .clr(button_1_out), .d0(in_1[7]), .d1(in_1[6]), .d2(in_1[5]), .d3(in_1[4]), .d4(in_1[3]), .d5(in_1[2]),
    .d6(in_1[1]), .d7(in_1[0]));  // open: q0, q1, q2, q3, q4, q5, q6, q7
  Clock clock_1 (.out(clock_1_out));
  Button button_1 (.out(button_1_out));
  LED led_1 (.in(shift_register_1_out));
endmodule
