// Logisim project hw1.circ as structural Verilog: 1 circuit, main circuit main
module main (
  input  [7:0] A,
  input  [7:0] B,
  input  [7:0] C
);

  wire Clock_out;
  wire [7:0] _8_Bit_Register_2_q, _8_Bit_Register_3_q, _8_Bit_Register_4_q, _8_Bit_Register_5_q,
       _8_Bit_Register_6_q, _8_Bit_Register_7_q, _8_Bit_Register_8_q, _8_Bit_Register_9_q, _8_Bit_Register_q,
       adder_1_out, adder_2_out, adder_3_out, multiplier_1_out, subtractor_1_out, subtractor_2_out,
       XOR_2_out, XOR_out;

  Clock Clock (.out(Clock_out));
  Register _8_Bit_Register (.D(A), .Q(_8_Bit_Register_q), .clk(Clock_out));  // open: en, clr
  Register _8_Bit_Register_2 (.D(B), .Q(_8_Bit_Register_2_q), .clk(Clock_out));  // open: en, clr
  Register _8_Bit_Register_3 (.D(C), .Q(_8_Bit_Register_3_q), .clk(Clock_out));  // open: en, clr
  Subtractor subtractor_1 (.a(_8_Bit_Register_q), .b(_8_Bit_Register_2_q), .out(subtractor_1_out));  // open: bin, bout
  Subtractor subtractor_2 (.a(_8_Bit_Register_q), .b(_8_Bit_Register_3_q), .out(subtractor_2_out));  // open: bin, bout
  Register _8_Bit_Register_4 (.D(XOR_out), .Q(_8_Bit_Register_4_q), .clk(Clock_out));  // open: en, clr
  assign XOR_out = subtractor_1_out ^ subtractor_1_out;  // XOR_Gate XOR, 8 bits wide
  assign XOR_2_out = subtractor_2_out ^ subtractor_2_out;  // XOR_Gate XOR_2, 8 bits wide
  Register _8_Bit_Register_5 (.D(XOR_2_out), .Q(_8_Bit_Register_5_q), .clk(Clock_out));  // open: en, clr
  Adder adder_1 (.a(subtractor_1_out), .b(_8_Bit_Register_4_q), .out(adder_1_out));  // open: cin, cout
  Adder adder_2 (.a(_8_Bit_Register_5_q), .b(subtractor_2_out), .out(adder_2_out));  // open: cin, cout
  Register _8_Bit_Register_6 (.D(adder_1_out), .Q(_8_Bit_Register_6_q), .clk(Clock_out));  // open: en, clr
  Register _8_Bit_Register_7 (.D(adder_2_out), .Q(_8_Bit_Register_7_q), .clk(Clock_out));  // open: en, clr
  Multiplier multiplier_1 (
    .a(_8_Bit_Register_2_q), .b(_8_Bit_Register_7_q), .out(multiplier_1_out));  // open: cin, cout
  Register _8_Bit_Register_8 (.D(_8_Bit_Register_6_q), .Q(_8_Bit_Register_8_q), .clk(Clock_out));  // open: en, clr
  Register _8_Bit_Register_9 (.D(multiplier_1_out), .Q(_8_Bit_Register_9_q), .clk(Clock_out));  // open: en, clr
  Adder adder_3 (.a(_8_Bit_Register_8_q), .b(_8_Bit_Register_9_q), .out(adder_3_out));  // open: cin, cout
  Register _16_Bit_Register__Output (.D(adder_3_out), .clk(Clock_out));  // open: en, Q, clr

  // Notes on the sheet:
  //   STAGE 1
  //   55
  //   Subtractor
  //   Subtractor
  //   STAGE 2
  //   MSB
  //   MSB
  //   40
  //   STAGE 3
  //   Adder
  //   Adder
  //   30
  //   STAGE 4
  //   Multiplicator
  //   40
  //   STAGE 5
  //   16-Bit Adder
  //   45
endmodule
